// Logisim project Aniol64keyboard.circ as structural Verilog: 1 circuit, main circuit main
module main (
  input  in_1,
  input  M1,
  input  IORQ,
  input  [6:0] in_4,
  input  IEI,
  input  in_6,
  input  A6,
  input  RD,
  output IEO,
  output Register_OE_prime,
  output INT
);

  wire and_1_out, clock_1_out, d_ff_1_q, d_ff_1_qn, not_1_out, or_1_out, or_2_out, or_3_out, or_4_out,
       pull_resistor_1_node, switch_1_p2, switch_1_p3, switch_1_p5, switch_1_p6, switch_1_p7;
  wire [6:0] counter_1_q;

  Clock clock_1 (.out(clock_1_out));
  Pull_Resistor pull_resistor_1 (.node(pull_resistor_1_node));
  or or_1 (or_1_out, in_6, A6);
  Counter #(.max('h7f), .width(7)) counter_1 (
    .clr(in_1), .clk(or_2_out), .Q(counter_1_q));  // open: load, up, count, D, carry
  or or_2 (or_2_out, clock_1_out, pull_resistor_1_node);
  or or_3 (or_3_out, or_1_out, RD);
  Register #(.width(7)) register_1 (.D(counter_1_q), .clk(and_1_out), .Q(in_4));  // open: en, clr
  Multiplexer #(.enable("false"), .select(3)) multiplexer_1 (
    .in2(switch_1_p6), .out(pull_resistor_1_node), .sel(counter_1_q[6:4]));  // open: in0, in1, in3, in4, in5, in6, in7
  LED led_1 (.in(pull_resistor_1_node));
  or or_4 (or_4_out, M1, IORQ);
  D_Flip_Flop d_ff_1 (
    .D(1'b1), .clk(pull_resistor_1_node), .Q(d_ff_1_q), .Qn(d_ff_1_qn), .reset(not_1_out));  // open: preset
  not not_1 (not_1_out, or_4_out);
  // Switch switch_1: pin names not known; wires that end beside it: IORQ, switch_1_p2, switch_1_p3, switch_1_p2, switch_1_p5, switch_1_p6, switch_1_p7, switch_1_p7
  and and_1 (and_1_out, d_ff_1_q, IEI);
  Demultiplexer #(.enable("false"), .select(4)) demultiplexer_1 (
    .out0(switch_1_p3), .out3(switch_1_p5), .in(1'b1), .sel(counter_1_q[3:0]));  // open: out1, out2, out4, out5, out6, out7, out8, out9, out10, out11, out12, out13, out14, out15
  and and_2 (IEO, d_ff_1_qn, IEI);
  not not_2 (INT, and_1_out);

  // Notes on the sheet:
  //   IORQ
  //   Interrupt Acknowledge
  //   D6-D0
endmodule
